# Fritzing sketch buzzer (saved by Fritzing 0.9.3b)

parts:
  Raspberry_Pi_1 = Raspberry Pi 3 [part_number=RPI-3-V1.2]
  J1 = Piezo Speaker

nets:
  N1: Raspberry_Pi_1.GND, J1.pin1
  N2: Raspberry_Pi_1.GPIO23, J1.pin2

notes:
  Pin 16
