# Fritzing sketch sensor (saved by Fritzing 0.9.3b)

parts:
  Componente1 = PIR D-SUN HC-SR501
  Raspberry_Pi_1 = Raspberry Pi 3 [part_number=RPI-3-V1.2]

nets:
  N1: Componente1.connector0, Raspberry_Pi_1.5V
  N2: Componente1.connector1, Raspberry_Pi_1.GPIO21
  N3: Componente1.connector2, Raspberry_Pi_1.GND

notes:
  Pin 40
